// Logisim project CircuitoParidadePar.circ as structural Verilog: 1 circuit, main circuit main
module main (
  input  A,
  input  B,
  input  C,
  input  I,
  input  D,
  input  A_2,
  input  B_2,
  input  C_2,
  input  D_2,
  input  A_3,
  input  I_2,
  input  B_3,
  input  A_4,
  input  C_3,
  input  B_4,
  input  D_3,
  input  C_4,
  input  D_4,
  output S,
  output A_s,
  output B_s,
  output C_s,
  output S_2,
  output D_s,
  output As,
  output Bs,
  output Cs,
  output Ds,
  output S_3,
  output S_4
);

  wire xor_1_out, xor_2_out, xor_3_out, xor_5_out, xor_7_out, xor_8_out, xor_9_out, xor_11_out, xor_12_out,
       xor_13_out;

  xor xor_1 (xor_1_out, A, B);
  xor xor_2 (xor_2_out, A_3, B_3);
  xor xor_3 (xor_3_out, C_3, xor_2_out);
  xor xor_4 (S_3, D_3, xor_3_out);
  xor xor_5 (xor_5_out, xor_1_out, C);
  xor xor_6 (S, xor_5_out, D);
  xor xor_7 (xor_7_out, I, A_2);
  xor xor_8 (xor_8_out, I_2, A_4);
  xor xor_9 (xor_9_out, C_4, xor_12_out);
  xor xor_10 (S_4, D_4, xor_9_out);
  xor xor_11 (xor_11_out, xor_7_out, B_2);
  xor xor_12 (xor_12_out, xor_8_out, B_4);
  xor xor_13 (xor_13_out, xor_11_out, C_2);
  xor xor_14 (S_2, xor_13_out, D_2);

  assign A_s = D;
  assign As = A_3;
  assign B_s = C;
  assign Bs = B_3;
  assign C_s = B;
  assign Cs = C_3;
  assign D_s = A;
  assign Ds = D_3;

  // Notes on the sheet:
  //   Gerador de Paridade Par
  //   Gerador Paridade Par
  //   Verificador de Paridade Par
  //   Verificador de Paridade Par
endmodule
