// Logisim project DecodificadorAtivoAlto2x4.circ as structural Verilog: 1 circuit, main circuit main
module main (
  input  A0,
  input  A1,
  output Q0,
  output Q1,
  output Q2,
  output Q3
);

  wire not_1_out, not_2_out;

  not not_1 (not_1_out, A0);
  not not_2 (not_2_out, A1);
  and and_1 (Q0, not_1_out, not_2_out);
  and and_2 (Q1, A0, not_2_out);
  and and_3 (Q2, not_1_out, A1);
  and and_4 (Q3, A0, A1);

  // Notes on the sheet:
  //   Decodificador ativo alto 2x4
endmodule
