// Logisim project DecodificadorBinDec.circ as structural Verilog: 1 circuit, main circuit main
module main (
  input  A,
  input  B,
  input  C,
  input  D,
  output S9,
  output S8,
  output S7,
  output S6,
  output S5,
  output S4,
  output S3,
  output S2,
  output S1,
  output S0
);

  wire not_1_out, not_2_out, not_3_out, not_4_out;

  not not_1 (not_1_out, A);
  not not_2 (not_2_out, C);
  not not_3 (not_3_out, B);
  not not_4 (not_4_out, D);
  and and_1 (S9, A, D);
  and and_2 (S8, A, not_4_out);
  and and_3 (S7, B, C, D);
  and and_4 (S6, B, C, not_4_out);
  and and_5 (S5, B, not_2_out, D);
  and and_6 (S4, B, not_2_out, not_4_out);
  and and_7 (S3, not_3_out, C, D);
  and and_8 (S2, not_3_out, C, not_4_out);
  and and_9 (S1, not_1_out, not_3_out, not_2_out, D);
  and and_10 (S0, not_1_out, not_3_out, not_2_out, not_4_out);

  // Notes on the sheet:
  //   Decodificador Binário Decimal
endmodule
