// Logisim project Display7segAndConverterDecToBin.circ as structural Verilog: 4 circuits, main circuit deco_bin_dec
module modulo (
  input  [3:0] in_1,
  input  [3:0] in_2,
  input  [9:0] in_3,
  input  [3:0] in_4,
  input  in_5,
  input  [9:0] in_6,
  input  in_7,
  output [9:0] out_8,
  output [9:0] out_9,
  output [3:0] out_10,
  output [9:0] out_11
);

  wire display_1_a_2, display_1_b_2, display_1_c_2, display_1_d_2, display_1_e, display_1_f, display_1_g,
       display_1_pt, display_2_a_2, display_2_b_2, display_2_c_2, display_2_d_2, display_2_e, display_2_f,
       display_2_g, display_2_pt;
  wire [3:0] priority_encoder_1_out;

  deco_bin_dec deco_bin_dec_1 (
    .S9(out_8[9]), .S8(out_8[8]), .S7(out_8[7]), .S6(out_8[6]), .S5(out_8[5]), .S4(out_8[4]), .S3(out_8[3]),
    .S2(out_8[2]), .S1(out_8[1]), .S0(out_8[0]), .A(in_1[3]), .B(in_1[2]), .C(in_1[1]), .D(in_1[0]));
  Decoder #(.select(4), .enable("false")) decoder_1 (
    .out0(out_9[0]), .out1(out_9[1]), .out2(out_9[2]), .out3(out_9[3]), .out4(out_9[4]), .out5(out_9[5]),
    .out6(out_9[6]), .out7(out_9[7]), .out8(out_9[8]), .out9(out_9[9]), .sel(in_4));  // open: out10, out11, out12, out13, out14, out15
  Priority_Encoder #(.select(4)) priority_encoder_1 (
    .in0(in_6[0]), .in1(in_6[1]), .in2(in_6[2]), .in3(in_6[3]), .in4(in_6[4]), .in5(in_6[5]), .in6(in_6[6]),
    .in7(in_6[7]), .in8(in_6[8]), .in9(in_6[9]), .out(priority_encoder_1_out), .en_in(in_7));  // open: in10, in11, in12, in13, in14, in15, gs, en_out
  Decoder #(.select(4), .enable("false")) decoder_2 (
    .out0(out_11[0]), .out1(out_11[1]), .out2(out_11[2]), .out3(out_11[3]), .out4(out_11[4]),
    .out5(out_11[5]), .out6(out_11[6]), .out7(out_11[7]), .out8(out_11[8]), .out9(out_11[9]),
    .sel(priority_encoder_1_out));  // open: out10, out11, out12, out13, out14, out15
  Display display_1 (
    .A(priority_encoder_1_out[3]), .B(priority_encoder_1_out[2]), .C(priority_encoder_1_out[1]),
    .D(priority_encoder_1_out[0]), .a_2(display_1_a_2), .b_2(display_1_b_2), .c_2(display_1_c_2),
    .d_2(display_1_d_2), .e(display_1_e), .f(display_1_f), .g(display_1_g), .pt(display_1_pt));
  _7_Segment_Display u_7_segment_display_1 (
    .g(display_1_g), .f(display_1_f), .a(display_1_a_2), .b(display_1_b_2), .e(display_1_e),
    .d(display_1_d_2), .c(display_1_c_2), .dp(display_1_pt));
  Display display_2 (
    .A(in_2[3]), .B(in_2[2]), .C(in_2[1]), .D(in_2[0]), .a_2(display_2_a_2), .b_2(display_2_b_2),
    .c_2(display_2_c_2), .d_2(display_2_d_2), .e(display_2_e), .f(display_2_f), .g(display_2_g),
    .pt(display_2_pt));
  _7_Segment_Display u_7_segment_display_2 (
    .g(display_2_g), .f(display_2_f), .a(display_2_a_2), .b(display_2_b_2), .e(display_2_e),
    .d(display_2_d_2), .c(display_2_c_2), .dp(display_2_pt));
  Priority_Encoder #(.select(4)) priority_encoder_2 (
    .in0(in_3[0]), .in1(in_3[1]), .in2(in_3[2]), .in3(in_3[3]), .in4(in_3[4]), .in5(in_3[5]), .in6(in_3[6]),
    .in7(in_3[7]), .in8(in_3[8]), .in9(in_3[9]), .out(out_10), .en_in(in_5));  // open: in10, in11, in12, in13, in14, in15, gs, en_out
endmodule

// A, B, C, D
module deco_bin_dec (
  input  A,
  input  B,
  input  C,
  input  D,
  output S9,
  output S8,
  output S7,
  output S6,
  output S5,
  output S4,
  output S3,
  output S2,
  output S1,
  output S0
);

  wire not_1_out, not_2_out, not_3_out, not_4_out;

  not not_1 (not_1_out, A);
  not not_2 (not_2_out, B);
  not not_3 (not_3_out, C);
  not not_4 (not_4_out, D);
  and and_1 (S9, A, D);
  and and_2 (S8, A, not_4_out);
  and and_3 (S7, B, C, D);
  and and_4 (S6, B, C, not_4_out);
  and and_5 (S5, B, not_3_out, D);
  and and_6 (S4, B, not_3_out, not_4_out);
  and and_7 (S3, not_2_out, C, D);
  and and_8 (S2, not_2_out, C, not_4_out);
  and and_9 (S1, not_1_out, not_2_out, not_3_out, D);
  and and_10 (S0, not_1_out, not_2_out, not_3_out, not_4_out);

  // Notes on the sheet:
  //   Decodificador Binário Decimal
endmodule

module Deco_bin_dec (
  input  A,
  input  B,
  input  C,
  input  D,
  output S9,
  output S8,
  output S7,
  output S6,
  output S5,
  output S4,
  output S3,
  output S2,
  output S1,
  output S0
);

  wire not_1_out, not_2_out, not_3_out, not_4_out, not_5_out, not_6_out, not_7_out, not_8_out, not_9_out,
       not_10_out, not_11_out, not_12_out, not_13_out, not_14_out, not_15_out, not_16_out, not_17_out,
       not_18_out, not_19_out, not_20_out, not_21_out, not_22_out, not_23_out, not_24_out, not_25_out;

  not not_1 (not_1_out, B);
  not not_2 (not_2_out, C);
  not not_3 (not_3_out, B);
  not not_4 (not_4_out, C);
  not not_5 (not_5_out, D);
  not not_6 (not_6_out, A);
  not not_7 (not_7_out, A);
  not not_8 (not_8_out, D);
  not not_9 (not_9_out, A);
  not not_10 (not_10_out, C);
  not not_11 (not_11_out, A);
  not not_12 (not_12_out, C);
  not not_13 (not_13_out, D);
  not not_14 (not_14_out, A);
  not not_15 (not_15_out, B);
  not not_16 (not_16_out, A);
  not not_17 (not_17_out, B);
  not not_18 (not_18_out, D);
  not not_19 (not_19_out, A);
  not not_20 (not_20_out, B);
  not not_21 (not_21_out, C);
  not not_22 (not_22_out, A);
  not not_23 (not_23_out, B);
  not not_24 (not_24_out, C);
  not not_25 (not_25_out, D);
  and and_1 (S9, A, not_1_out, not_2_out, D);
  and and_2 (S8, A, not_3_out, not_4_out, not_5_out);
  and and_3 (S7, not_6_out, B, C, D);
  and and_4 (S6, not_7_out, B, C, not_8_out);
  and and_5 (S5, not_9_out, B, not_10_out, D);
  and and_6 (S4, not_11_out, B, not_12_out, not_13_out);
  and and_7 (S3, not_14_out, not_15_out, C, D);
  and and_8 (S2, not_16_out, not_17_out, C, not_18_out);
  and and_9 (S1, not_19_out, not_20_out, not_21_out, D);
  and and_10 (S0, not_22_out, not_23_out, not_24_out, not_25_out);
endmodule

module Display (
  input  A,
  input  B,
  input  C,
  input  D,
  output a_2,
  output b_2,
  output c_2,
  output d_2,
  output e,
  output f,
  output g,
  output pt
);

  wire and_1_out, and_2_out, and_3_out, and_4_out, and_5_out, and_6_out, and_7_out, and_8_out, and_9_out,
       and_10_out, and_11_out, and_12_out, and_13_out, and_14_out, and_15_out, and_16_out, and_17_out,
       and_18_out, and_19_out, and_20_out, and_21_out, and_22_out, and_23_out, and_24_out, and_25_out,
       and_26_out, and_27_out, and_28_out, not_1_out, not_2_out, not_3_out, not_4_out, not_5_out, not_6_out,
       not_7_out, not_8_out, not_9_out, not_10_out, not_11_out, not_12_out, not_13_out, not_14_out,
       not_15_out, not_16_out, not_17_out, not_18_out, not_19_out, not_20_out, not_21_out, not_22_out,
       not_23_out, not_24_out, not_25_out, not_26_out, not_27_out, not_28_out, not_29_out, not_30_out,
       not_31_out, not_32_out, not_33_out, not_34_out, not_35_out, not_36_out, not_37_out, not_38_out,
       not_39_out, not_40_out, not_41_out, not_42_out, not_43_out, not_44_out, not_45_out, not_46_out,
       not_47_out, not_48_out, not_49_out, not_50_out, not_51_out, not_52_out;

  not not_1 (not_1_out, A);
  not not_2 (not_2_out, B);
  and and_1 (and_1_out, not_1_out, not_2_out, not_3_out);
  not not_3 (not_3_out, D);
  not not_4 (not_4_out, A);
  and and_2 (and_2_out, not_4_out, C);
  not not_5 (not_5_out, A);
  and and_3 (and_3_out, not_5_out, B, D);
  and and_4 (and_4_out, A, not_6_out, not_7_out);
  not not_6 (not_6_out, B);
  not not_7 (not_7_out, C);
  not not_8 (not_8_out, A);
  and and_5 (and_5_out, not_8_out, not_9_out);
  not not_9 (not_9_out, B);
  not not_10 (not_10_out, A);
  not not_11 (not_11_out, C);
  and and_6 (and_6_out, not_10_out, not_11_out, not_12_out);
  not not_12 (not_12_out, D);
  not not_13 (not_13_out, B);
  and and_7 (and_7_out, not_13_out, not_14_out);
  not not_14 (not_14_out, C);
  not not_15 (not_15_out, A);
  and and_8 (and_8_out, not_15_out, C, D);
  not not_16 (not_16_out, B);
  and and_9 (and_9_out, not_16_out, not_17_out);
  not not_17 (not_17_out, C);
  not not_18 (not_18_out, A);
  and and_10 (and_10_out, not_18_out, D);
  not not_19 (not_19_out, A);
  and and_11 (and_11_out, not_19_out, B);
  not not_20 (not_20_out, A);
  not not_21 (not_21_out, B);
  not not_22 (not_22_out, D);
  not not_23 (not_23_out, A);
  not not_24 (not_24_out, B);
  not not_25 (not_25_out, A);
  not not_26 (not_26_out, D);
  not not_27 (not_27_out, A);
  not not_28 (not_28_out, C);
  not not_29 (not_29_out, B);
  not not_30 (not_30_out, C);
  not not_31 (not_31_out, B);
  not not_32 (not_32_out, C);
  and and_12 (and_12_out, not_31_out, not_32_out, not_33_out);
  not not_33 (not_33_out, D);
  not not_34 (not_34_out, A);
  and and_13 (and_13_out, not_34_out, C, not_35_out);
  not not_35 (not_35_out, D);
  not not_36 (not_36_out, A);
  not not_37 (not_37_out, C);
  and and_14 (and_14_out, not_36_out, not_37_out, not_38_out);
  not not_38 (not_38_out, D);
  not not_39 (not_39_out, A);
  and and_15 (and_15_out, not_39_out, B, not_40_out);
  not not_40 (not_40_out, C);
  not not_41 (not_41_out, A);
  and and_16 (and_16_out, not_41_out, B, not_42_out);
  not not_42 (not_42_out, D);
  not not_43 (not_43_out, B);
  and and_17 (and_17_out, A, not_43_out, not_44_out);
  not not_44 (not_44_out, C);
  not not_45 (not_45_out, A);
  not not_46 (not_46_out, B);
  and and_18 (and_18_out, not_45_out, not_46_out, C);
  not not_47 (not_47_out, A);
  and and_19 (and_19_out, not_47_out, B, not_48_out);
  not not_48 (not_48_out, C);
  not not_49 (not_49_out, A);
  and and_20 (and_20_out, not_49_out, B, not_50_out);
  not not_50 (not_50_out, D);
  not not_51 (not_51_out, B);
  and and_21 (and_21_out, A, not_51_out, not_52_out);
  not not_52 (not_52_out, C);
  and and_22 (and_22_out, A, C);
  and and_23 (and_23_out, A, B);
  or or_1 (a_2, and_1_out, and_2_out, and_3_out, and_4_out);
  or or_2 (b_2, and_5_out, and_6_out, and_7_out, and_8_out);
  or or_3 (c_2, and_9_out, and_10_out, and_11_out);
  and and_24 (and_24_out, not_20_out, not_21_out, not_22_out);
  and and_25 (and_25_out, not_23_out, not_24_out, C);
  and and_26 (and_26_out, not_25_out, C, not_26_out);
  and and_27 (and_27_out, not_27_out, B, not_28_out, D);
  and and_28 (and_28_out, A, not_29_out, not_30_out);
  or or_4 (e, and_12_out, and_13_out);
  or or_5 (f, and_14_out, and_15_out, and_16_out, and_17_out);
  or or_6 (g, and_18_out, and_19_out, and_20_out, and_21_out);
  or or_7 (pt, and_22_out, and_23_out);
  or or_8 (d_2, and_24_out, and_25_out, and_26_out, and_27_out, and_28_out);
endmodule
