// Logisim project Stopwatch99to0flipflopJK.circ as structural Verilog: 5 circuits, main circuit ci_display
module ci_display (
  input  A,
  input  B,
  input  C,
  input  D,
  output a_2,
  output b_2,
  output c_2,
  output d_2,
  output e,
  output f,
  output g,
  output pt
);

  wire and_1_out, and_2_out, and_3_out, and_4_out, and_5_out, and_6_out, and_7_out, and_8_out, and_9_out,
       and_10_out, and_11_out, and_12_out, and_13_out, and_14_out, and_15_out, and_16_out, and_17_out,
       and_18_out, and_19_out, and_20_out, and_21_out, and_22_out, and_23_out, and_24_out, and_25_out,
       and_26_out, and_27_out, and_28_out, not_1_out, not_2_out, not_3_out, not_4_out, not_5_out, not_6_out,
       not_7_out, not_8_out, not_9_out, not_10_out, not_11_out, not_12_out, not_13_out, not_14_out,
       not_15_out, not_16_out, not_17_out, not_18_out, not_19_out, not_20_out, not_21_out, not_22_out,
       not_23_out, not_24_out, not_25_out, not_26_out, not_27_out, not_28_out, not_29_out, not_30_out,
       not_31_out, not_32_out, not_33_out, not_34_out, not_35_out, not_36_out, not_37_out, not_38_out,
       not_39_out, not_40_out, not_41_out, not_42_out, not_43_out, not_44_out, not_45_out, not_46_out,
       not_47_out, not_48_out, not_49_out, not_50_out, not_51_out, not_52_out;

  not not_1 (not_1_out, A);
  and and_1 (and_1_out, not_1_out, not_2_out, not_3_out);
  not not_2 (not_2_out, B);
  not not_3 (not_3_out, D);
  not not_4 (not_4_out, A);
  and and_2 (and_2_out, not_4_out, C);
  not not_5 (not_5_out, A);
  and and_3 (and_3_out, not_5_out, B, D);
  and and_4 (and_4_out, A, not_6_out, not_7_out);
  not not_6 (not_6_out, B);
  not not_7 (not_7_out, C);
  not not_8 (not_8_out, A);
  and and_5 (and_5_out, not_8_out, not_9_out);
  not not_9 (not_9_out, B);
  not not_10 (not_10_out, A);
  not not_11 (not_11_out, C);
  and and_6 (and_6_out, not_10_out, not_11_out, not_12_out);
  not not_12 (not_12_out, D);
  not not_13 (not_13_out, B);
  and and_7 (and_7_out, not_13_out, not_14_out);
  not not_14 (not_14_out, C);
  not not_15 (not_15_out, A);
  and and_8 (and_8_out, not_15_out, C, D);
  not not_16 (not_16_out, B);
  and and_9 (and_9_out, not_16_out, not_17_out);
  not not_17 (not_17_out, C);
  not not_18 (not_18_out, A);
  and and_10 (and_10_out, not_18_out, D);
  not not_19 (not_19_out, A);
  and and_11 (and_11_out, not_19_out, B);
  not not_20 (not_20_out, A);
  not not_21 (not_21_out, B);
  not not_22 (not_22_out, D);
  not not_23 (not_23_out, A);
  not not_24 (not_24_out, B);
  not not_25 (not_25_out, A);
  not not_26 (not_26_out, D);
  not not_27 (not_27_out, A);
  not not_28 (not_28_out, C);
  not not_29 (not_29_out, B);
  not not_30 (not_30_out, C);
  not not_31 (not_31_out, B);
  not not_32 (not_32_out, C);
  and and_12 (and_12_out, not_31_out, not_32_out, not_33_out);
  not not_33 (not_33_out, D);
  not not_34 (not_34_out, A);
  and and_13 (and_13_out, not_34_out, C, not_35_out);
  not not_35 (not_35_out, D);
  not not_36 (not_36_out, A);
  and and_14 (and_14_out, not_36_out, not_37_out, not_38_out);
  not not_37 (not_37_out, C);
  not not_38 (not_38_out, D);
  not not_39 (not_39_out, A);
  and and_15 (and_15_out, not_39_out, B, not_40_out);
  not not_40 (not_40_out, C);
  not not_41 (not_41_out, A);
  and and_16 (and_16_out, not_41_out, B, not_42_out);
  not not_42 (not_42_out, D);
  and and_17 (and_17_out, A, not_43_out, not_44_out);
  not not_43 (not_43_out, B);
  not not_44 (not_44_out, C);
  not not_45 (not_45_out, A);
  not not_46 (not_46_out, B);
  and and_18 (and_18_out, not_45_out, not_46_out, C);
  not not_47 (not_47_out, A);
  and and_19 (and_19_out, not_47_out, B, not_48_out);
  not not_48 (not_48_out, C);
  not not_49 (not_49_out, A);
  and and_20 (and_20_out, not_49_out, B, not_50_out);
  not not_50 (not_50_out, D);
  not not_51 (not_51_out, B);
  and and_21 (and_21_out, A, not_51_out, not_52_out);
  not not_52 (not_52_out, C);
  and and_22 (and_22_out, A, C);
  and and_23 (and_23_out, A, B);
  or or_1 (a_2, and_1_out, and_2_out, and_3_out, and_4_out);
  or or_2 (b_2, and_5_out, and_6_out, and_7_out, and_8_out);
  or or_3 (c_2, and_9_out, and_10_out, and_11_out);
  and and_24 (and_24_out, not_20_out, not_21_out, not_22_out);
  and and_25 (and_25_out, not_23_out, not_24_out, C);
  and and_26 (and_26_out, not_25_out, C, not_26_out);
  and and_27 (and_27_out, not_27_out, B, not_28_out, D);
  and and_28 (and_28_out, A, not_29_out, not_30_out);
  or or_4 (e, and_12_out, and_13_out);
  or or_5 (f, and_14_out, and_15_out, and_16_out, and_17_out);
  or or_6 (g, and_18_out, and_19_out, and_20_out, and_21_out);
  or or_7 (pt, and_22_out, and_23_out);
  or or_8 (d_2, and_24_out, and_25_out, and_26_out, and_27_out, and_28_out);

  // Notes on the sheet:
  //   Anderson Carlos da Silva Morais - 2020010461
endmodule

module ci_contador (
  output [3:0] unidade,
  output [3:0] dezena
);

  wire and_1_out, and_2_out, clock_1_out, j_k_ff_1_qn, j_k_ff_2_q, j_k_ff_2_qn, j_k_ff_3_qn, j_k_ff_4_q,
       j_k_ff_4_qn, j_k_ff_5_q, j_k_ff_5_qn, j_k_ff_6_qn, j_k_ff_7_qn, j_k_ff_8_q, j_k_ff_8_qn;

  Clock clock_1 (.out(clock_1_out));
  J_K_Flip_Flop j_k_ff_1 (
    .J(1'b1), .clk(clock_1_out), .K(1'b1), .Qn(j_k_ff_1_qn), .en(1'b1), .reset(and_1_out));  // open: Q, preset
  J_K_Flip_Flop j_k_ff_2 (
    .J(1'b1), .clk(j_k_ff_1_qn), .K(1'b1), .Q(j_k_ff_2_q), .Qn(j_k_ff_2_qn), .en(1'b1), .reset(and_1_out));  // open: preset
  J_K_Flip_Flop j_k_ff_3 (
    .J(1'b1), .clk(j_k_ff_2_qn), .K(1'b1), .Qn(j_k_ff_3_qn), .en(1'b1), .reset(and_1_out));  // open: Q, preset
  J_K_Flip_Flop j_k_ff_4 (
    .J(1'b1), .clk(j_k_ff_3_qn), .K(1'b1), .Q(j_k_ff_4_q), .Qn(j_k_ff_4_qn), .en(1'b1), .reset(and_1_out));  // open: preset
  ci_16p9 ci_16p9_1 (
    .a(j_k_ff_4_qn), .b(j_k_ff_3_qn), .c(j_k_ff_2_qn), .d(j_k_ff_1_qn), .s1(unidade[3]), .s2(unidade[2]),
    .s3(unidade[1]), .s4(unidade[0]));
  and and_1 (and_1_out, j_k_ff_4_q, j_k_ff_2_q);
  J_K_Flip_Flop j_k_ff_5 (
    .J(1'b1), .clk(j_k_ff_4_qn), .K(1'b1), .Q(j_k_ff_5_q), .Qn(j_k_ff_5_qn), .en(1'b1), .reset(and_2_out));  // open: preset
  J_K_Flip_Flop j_k_ff_6 (
    .J(1'b1), .clk(j_k_ff_5_qn), .K(1'b1), .Qn(j_k_ff_6_qn), .en(1'b1), .reset(and_2_out));  // open: Q, preset
  J_K_Flip_Flop j_k_ff_7 (
    .J(1'b1), .clk(j_k_ff_6_qn), .K(1'b1), .Qn(j_k_ff_7_qn), .en(1'b1), .reset(and_2_out));  // open: Q, preset
  J_K_Flip_Flop j_k_ff_8 (
    .J(1'b1), .clk(j_k_ff_7_qn), .K(1'b1), .Q(j_k_ff_8_q), .Qn(j_k_ff_8_qn), .en(1'b1), .reset(and_2_out));  // open: preset
  ci_16p9 ci_16p9_2 (
    .a(j_k_ff_8_qn), .b(j_k_ff_7_qn), .c(j_k_ff_6_qn), .d(j_k_ff_5_qn), .s1(dezena[3]), .s2(dezena[2]),
    .s3(dezena[1]), .s4(dezena[0]));
  and and_2 (and_2_out, j_k_ff_8_q, j_k_ff_5_q);

  // Notes on the sheet:
  //   Anderson Carlos da Silva Morais - 2020010461
endmodule

module ci_distribuidor (
  output [3:0] _1_up,
  output [3:0] _1dwn,
  output [3:0] _10up,
  output [3:0] _10dwn
);

  wire [3:0] Circuito_do_contador_dezena, Circuito_do_contador_unidade;

  ci_contador Circuito_do_contador (.unidade(Circuito_do_contador_unidade), .dezena(Circuito_do_contador_dezena));
  ci_display unidade (
    .A(Circuito_do_contador_unidade[3]), .B(Circuito_do_contador_unidade[2]),
    .C(Circuito_do_contador_unidade[1]), .D(Circuito_do_contador_unidade[0]), .a_2(_1_up[1]), .b_2(_1_up[0]),
    .c_2(_1dwn[2]), .d_2(_1dwn[1]), .e(_1dwn[0]), .f(_1_up[2]), .g(_1_up[3]), .pt(_1dwn[3]));
  ci_display dezena (
    .A(Circuito_do_contador_dezena[3]), .B(Circuito_do_contador_dezena[2]),
    .C(Circuito_do_contador_dezena[1]), .D(Circuito_do_contador_dezena[0]), .a_2(_10up[1]), .b_2(_10up[0]),
    .c_2(_10dwn[2]), .d_2(_10dwn[1]), .e(_10dwn[0]), .f(_10up[2]), .g(_10up[3]), .pt(_10dwn[3]));

  // Notes on the sheet:
  //   Circuito distribuidor
  //   Anderson Carlos da Silva Morais - 2020010461
endmodule

module mostrador (
);

  wire [3:0] Circuito_distribuidor__1_up, Circuito_distribuidor__1dwn, Circuito_distribuidor__10dwn,
       Circuito_distribuidor__10up;

  ci_distribuidor Circuito_distribuidor (
    ._1_up(Circuito_distribuidor__1_up), ._1dwn(Circuito_distribuidor__1dwn),
    ._10up(Circuito_distribuidor__10up), ._10dwn(Circuito_distribuidor__10dwn));
  _7_Segment_Display u_7_segment_display_1 (
    .g(Circuito_distribuidor__10up[3]), .f(Circuito_distribuidor__10up[2]),
    .a(Circuito_distribuidor__10up[1]), .b(Circuito_distribuidor__10up[0]),
    .e(Circuito_distribuidor__10dwn[0]), .d(Circuito_distribuidor__10dwn[1]),
    .c(Circuito_distribuidor__10dwn[2]), .dp(Circuito_distribuidor__10dwn[3]));
  _7_Segment_Display u_7_segment_display_2 (
    .g(Circuito_distribuidor__1_up[3]), .f(Circuito_distribuidor__1_up[2]),
    .a(Circuito_distribuidor__1_up[1]), .b(Circuito_distribuidor__1_up[0]),
    .e(Circuito_distribuidor__1dwn[0]), .d(Circuito_distribuidor__1dwn[1]),
    .c(Circuito_distribuidor__1dwn[2]), .dp(Circuito_distribuidor__1dwn[3]));

  // Notes on the sheet:
  //   Anderson Carlos da Silva Morais - 2020010461
  //   mostrador
endmodule

module ci_16p9 (
  input  a,
  input  b,
  input  c,
  input  d,
  output s1,
  output s2,
  output s3,
  output s4
);

  wire and_2_out, and_3_out, not_1_out, not_2_out;

  and and_1 (s1, a, b, c);
  not not_1 (not_1_out, b);
  not not_2 (not_2_out, c);
  not not_3 (s3, c);
  and and_2 (and_2_out, not_1_out, c);
  and and_3 (and_3_out, b, not_2_out);
  or or_1 (s2, and_2_out, and_3_out);

  assign s4 = d;

  // Notes on the sheet:
  //   Anderson Carlos da Silva Morais - 2020010461
  //   Circuito que codifica as 10 últimas saídas de 16 com os dígitos de 9 a 0
endmodule
