// Logisim project ULA_final.circ as structural Verilog: 9 circuits, main circuit main
module main (
  input  in_1,
  input  in_2,
  input  in_3,
  input  [3:0] A,
  input  [3:0] B,
  output [3:0] S
);

  ULA ula_1 (.A(A), .B(B), .in_3(in_1), .in_4(in_2), .in_5(in_3), .S(S));

  // Notes on the sheet:
  //   A=1011
  //   B=0111
  //   CODIGO - 110
  //   S=0001
endmodule

module IncrementadorDecrementador (
  input  Decrementar,
  input  A3,
  input  A2,
  input  A1,
  input  A0,
  output S3,
  output S2,
  output S1,
  output S0
);

  wire not_1_out;

  SomadorSubtrator somadorsubtrator_1 (
    .SUB(Decrementar), .A0(A0), .B0(not_1_out), .A1(A1), .B1(1'b0), .A2(A2), .B2(1'b0), .A3(A3), .B3(1'b0),
    .S0(S0), .S1(S1), .S2(S2), .S3(S3));  // open: out_14
  not not_1 (not_1_out, 1'b0);
endmodule

module Comparador (
  input  A3,
  input  A2,
  input  A1,
  input  A0,
  input  B3,
  input  B2,
  input  B1,
  input  B0,
  output A___B,
  output A___B_2,
  output A___B_3
);

  wire and_2_out, and_3_out, and_4_out, and_5_out, and_6_out, and_7_out, and_8_out, and_9_out, nand_1_out,
       nor_1_out, not_1_out, not_2_out, not_3_out, not_4_out, not_5_out, not_6_out, not_7_out, not_8_out,
       xnor_1_out, xnor_2_out, xnor_3_out, xnor_4_out, xnor_5_out, xnor_6_out, xnor_7_out, xnor_8_out,
       xnor_9_out, xnor_10_out, xnor_11_out, xnor_12_out, xnor_13_out, xnor_14_out, xnor_15_out, xnor_16_out,
       xnor_17_out, xnor_18_out, xnor_19_out, xnor_20_out;

  xnor xnor_1 (xnor_1_out, A3, B3);
  xnor xnor_2 (xnor_2_out, A2, B2);
  xnor xnor_3 (xnor_3_out, A1, B1);
  xnor xnor_4 (xnor_4_out, A0, B0);
  not not_1 (not_1_out, B3);
  xnor xnor_5 (xnor_5_out, A3, B3);
  not not_2 (not_2_out, B2);
  xnor xnor_6 (xnor_6_out, A3, B3);
  xnor xnor_7 (xnor_7_out, A2, B2);
  not not_3 (not_3_out, B1);
  xnor xnor_8 (xnor_8_out, A3, B3);
  xnor xnor_9 (xnor_9_out, A2, B2);
  xnor xnor_10 (xnor_10_out, A1, B1);
  not not_4 (not_4_out, B0);
  not not_5 (not_5_out, B3);
  xnor xnor_11 (xnor_11_out, A3, B3);
  not not_6 (not_6_out, B2);
  xnor xnor_12 (xnor_12_out, A3, B3);
  xnor xnor_13 (xnor_13_out, A2, B2);
  not not_7 (not_7_out, B1);
  xnor xnor_14 (xnor_14_out, A3, B3);
  xnor xnor_15 (xnor_15_out, A2, B2);
  xnor xnor_16 (xnor_16_out, A1, B1);
  not not_8 (not_8_out, B0);
  and and_1 (A___B, xnor_1_out, xnor_2_out, xnor_3_out, xnor_4_out);
  and and_2 (and_2_out, A3, not_1_out);
  and and_3 (and_3_out, xnor_5_out, A2, not_2_out);
  and and_4 (and_4_out, xnor_6_out, xnor_7_out, A1, not_3_out);
  and and_5 (and_5_out, xnor_8_out, xnor_9_out, xnor_10_out, A0, not_4_out);
  xnor xnor_17 (xnor_17_out, A3, B3);
  xnor xnor_18 (xnor_18_out, A2, B2);
  xnor xnor_19 (xnor_19_out, A1, B1);
  xnor xnor_20 (xnor_20_out, A0, B0);
  and and_6 (and_6_out, A3, not_5_out);
  and and_7 (and_7_out, xnor_11_out, A2, not_6_out);
  and and_8 (and_8_out, xnor_12_out, xnor_13_out, A1, not_7_out);
  and and_9 (and_9_out, xnor_14_out, xnor_15_out, xnor_16_out, A0, not_8_out);
  or or_1 (A___B_2, and_2_out, and_3_out, and_4_out, and_5_out);
  nand nand_1 (nand_1_out, xnor_17_out, xnor_18_out, xnor_19_out, xnor_20_out);
  nor nor_1 (nor_1_out, and_6_out, and_7_out, and_8_out, and_9_out);
  and and_10 (A___B_3, nand_1_out, nor_1_out);
endmodule

module Adder (
  input  a,
  input  b,
  output s,
  output carry
);

  xor xor_1 (s, a, b);
  and and_1 (carry, a, b);
endmodule

module FullAdder (
  input  C_in,
  input  A0,
  input  B0,
  output S,
  output C_out
);

  wire and_1_out, and_2_out, xor_1_out;

  xor xor_1 (xor_1_out, A0, B0);
  and and_1 (and_1_out, A0, B0);
  xor xor_2 (S, C_in, xor_1_out);
  and and_2 (and_2_out, C_in, xor_1_out);
  or or_1 (C_out, and_2_out, and_1_out);
endmodule

module SomadorSubtrator (
  input  SUB,
  input  A0,
  input  B0,
  input  A1,
  input  B1,
  input  A2,
  input  B2,
  input  A3,
  input  B3,
  output S0,
  output S1,
  output S2,
  output S3,
  output out_14
);

  wire fulladder_1_c_out, fulladder_2_c_out, fulladder_3_c_out, xor_1_out, xor_2_out, xor_3_out, xor_4_out;

  xor xor_1 (xor_1_out, B0, SUB);
  xor xor_2 (xor_2_out, B1, SUB);
  xor xor_3 (xor_3_out, B2, SUB);
  xor xor_4 (xor_4_out, B3, SUB);
  FullAdder fulladder_1 (.C_in(SUB), .A0(A0), .B0(xor_1_out), .S(S0), .C_out(fulladder_1_c_out));
  FullAdder fulladder_2 (.C_in(fulladder_1_c_out), .A0(A1), .B0(xor_2_out), .S(S1), .C_out(fulladder_2_c_out));
  FullAdder fulladder_3 (.C_in(fulladder_2_c_out), .A0(A2), .B0(xor_3_out), .S(S2), .C_out(fulladder_3_c_out));
  FullAdder fulladder_4 (.C_in(fulladder_3_c_out), .A0(A3), .B0(xor_4_out), .S(S3), .C_out(out_14));

  // Notes on the sheet:
  //   A = 1010
  //   B = 0011
  //   S = A - B = 0111
endmodule

module RascunhoFinal (
  input  [3:0] in_1,
  input  [3:0] in_2,
  input  in_3,
  input  in_4,
  input  \Operações ,
  output [3:0] out_6
);

  wire comparador_1_a___b, comparador_1_a___b_2, comparador_1_a___b_3;
  wire [3:0] incrementadordecrementador_1_s0, somadorsubtrator_1_s0, undriven;

  auxiliar auxiliar_1 ();  // open: a, b, c, s, s2
  SomadorSubtrator somadorsubtrator_1 (
    .SUB(\Operações ), .A0(in_1[0]), .B0(in_2[0]), .A1(in_1[1]), .B1(in_2[1]), .A2(in_1[2]), .B2(in_2[2]),
    .A3(in_1[3]), .B3(in_2[3]), .S0(somadorsubtrator_1_s0[0]), .S1(somadorsubtrator_1_s0[1]),
    .S2(somadorsubtrator_1_s0[2]), .S3(somadorsubtrator_1_s0[3]));  // open: out_14
  Comparador comparador_1 (
    .A3(in_1[3]), .A2(in_1[2]), .A1(in_1[1]), .A0(in_1[0]), .B3(in_2[3]), .B2(in_2[2]), .B1(in_2[1]),
    .B0(in_2[0]), .A___B(comparador_1_a___b), .A___B_2(comparador_1_a___b_2), .A___B_3(comparador_1_a___b_3));
  IncrementadorDecrementador incrementadordecrementador_1 (
    .Decrementar(\Operações ), .A3(in_1[3]), .A2(in_1[2]), .A1(in_1[1]), .A0(in_1[0]),
    .S3(incrementadordecrementador_1_s0[3]), .S2(incrementadordecrementador_1_s0[2]),
    .S1(incrementadordecrementador_1_s0[1]), .S0(incrementadordecrementador_1_s0[0]));
  // Multiplexer #(.select(2), .enable("false")) multiplexer_1: pin names not known; wires that end beside it: comparador_1_a___b, comparador_1_a___b_2, comparador_1_a___b_3
  Multiplexer #(.select(3), .width(4), .enable("false")) multiplexer_2 (
    .in0(somadorsubtrator_1_s0), .in1(somadorsubtrator_1_s0), .in2(incrementadordecrementador_1_s0),
    .in3(incrementadordecrementador_1_s0), .in4(undriven), .in5(undriven), .in6(undriven), .out(out_6),
    .sel({in_3, in_4, \Operações }));  // open: in7

  // Notes on the sheet:
  //   0000 - somar A + B
  //   0001 - subtrair A - B
  //   0010 - incrementar A
  //   0011 - decrementar A
  //   0100 - Comparação de A por B
  //   Subtrair?
  //   Decrementar?
  //   Somador e Subtrator
  //   Comparador
  //   Incremendor e Decrementador
endmodule

module auxiliar (
  input  a,
  input  b,
  input  c,
  output s,
  output s2
);

  wire and_1_out, and_2_out, not_1_out;

  not not_1 (not_1_out, a);
  and and_1 (and_1_out, not_1_out, c);
  and and_2 (and_2_out, a, b);
  or or_1 (s, and_1_out, and_2_out);

  assign s2 = c;
endmodule

module ULA (
  input  [3:0] A,
  input  [3:0] B,
  input  in_3,
  input  in_4,
  input  in_5,
  output [3:0] S
);

  wire comparador_1_a___b, comparador_1_a___b_2, comparador_1_a___b_3;
  wire [0:0] multiplexer_1_out;
  wire [1:0] auxiliar_1_s;
  wire [3:0] incrementadordecrementador_1_s0, somadorsubtrator_1_s0;

  auxiliar auxiliar_1 (.a(in_3), .b(in_4), .c(in_5), .s(auxiliar_1_s[0]), .s2(auxiliar_1_s[1]));
  SomadorSubtrator somadorsubtrator_1 (
    .SUB(auxiliar_1_s[0]), .A0(A[0]), .B0(B[0]), .A1(A[1]), .B1(B[1]), .A2(A[2]), .B2(B[2]), .A3(A[3]),
    .B3(B[3]), .S0(somadorsubtrator_1_s0[0]), .S1(somadorsubtrator_1_s0[1]), .S2(somadorsubtrator_1_s0[2]),
    .S3(somadorsubtrator_1_s0[3]));  // open: out_14
  Comparador comparador_1 (
    .A3(A[3]), .A2(A[2]), .A1(A[1]), .A0(A[0]), .B3(B[3]), .B2(B[2]), .B1(B[1]), .B0(B[0]),
    .A___B(comparador_1_a___b), .A___B_2(comparador_1_a___b_2), .A___B_3(comparador_1_a___b_3));
  IncrementadorDecrementador incrementadordecrementador_1 (
    .Decrementar(auxiliar_1_s[0]), .A3(A[3]), .A2(A[2]), .A1(A[1]), .A0(A[0]),
    .S3(incrementadordecrementador_1_s0[3]), .S2(incrementadordecrementador_1_s0[2]),
    .S1(incrementadordecrementador_1_s0[1]), .S0(incrementadordecrementador_1_s0[0]));
  Multiplexer #(.select(2), .enable("false")) multiplexer_1 (
    .in0(comparador_1_a___b), .in1(comparador_1_a___b_2), .in2(comparador_1_a___b_3), .in3(1'b0),
    .out(multiplexer_1_out[0]), .sel(auxiliar_1_s));
  Multiplexer #(.select(3), .width(4), .enable("false")) multiplexer_2 (
    .in0(somadorsubtrator_1_s0), .in1(somadorsubtrator_1_s0), .in2(incrementadordecrementador_1_s0),
    .in3(incrementadordecrementador_1_s0), .in4({3'b000, multiplexer_1_out[0]}),
    .in5({3'b000, multiplexer_1_out[0]}), .in6({3'b000, multiplexer_1_out[0]}), .out(S),
    .sel({in_3, in_4, in_5}));  // open: in7

  // Notes on the sheet:
  //   Operações
  //   000 - somar A + B
  //   001 - subtrair A - B
  //   010 - incrementar A
  //   011 - decrementar A
  //   100 - Comparação de A = B
  //   101 - Comparação de A < B
  //   110 - Comparação de A > B
  //   Auxiliar
  //   Subtrair?
  //   Decrementar?
endmodule
