// Logisim project Watch24FlipflopJK.circ as structural Verilog: 4 circuits, main circuit ci_display
module ci_display (
  input  A,
  input  B,
  input  C,
  input  D,
  output a_2,
  output b_2,
  output c_2,
  output d_2,
  output e,
  output f,
  output g,
  output pt
);

  wire and_1_out, and_2_out, and_3_out, and_4_out, and_5_out, and_6_out, and_7_out, and_8_out, and_9_out,
       and_10_out, and_11_out, and_12_out, and_13_out, and_14_out, and_15_out, and_16_out, and_17_out,
       and_18_out, and_19_out, and_20_out, and_21_out, and_22_out, and_23_out, and_24_out, and_25_out,
       and_26_out, and_27_out, and_28_out, not_1_out, not_2_out, not_3_out, not_4_out, not_5_out, not_6_out,
       not_7_out, not_8_out, not_9_out, not_10_out, not_11_out, not_12_out, not_13_out, not_14_out,
       not_15_out, not_16_out, not_17_out, not_18_out, not_19_out, not_20_out, not_21_out, not_22_out,
       not_23_out, not_24_out, not_25_out, not_26_out, not_27_out, not_28_out, not_29_out, not_30_out,
       not_31_out, not_32_out, not_33_out, not_34_out, not_35_out, not_36_out, not_37_out, not_38_out,
       not_39_out, not_40_out, not_41_out, not_42_out, not_43_out, not_44_out, not_45_out, not_46_out,
       not_47_out, not_48_out, not_49_out, not_50_out, not_51_out, not_52_out;

  not not_1 (not_1_out, A);
  and and_1 (and_1_out, not_1_out, not_2_out, not_3_out);
  not not_2 (not_2_out, B);
  not not_3 (not_3_out, D);
  not not_4 (not_4_out, A);
  and and_2 (and_2_out, not_4_out, C);
  not not_5 (not_5_out, A);
  and and_3 (and_3_out, not_5_out, B, D);
  and and_4 (and_4_out, A, not_6_out, not_7_out);
  not not_6 (not_6_out, B);
  not not_7 (not_7_out, C);
  not not_8 (not_8_out, A);
  and and_5 (and_5_out, not_8_out, not_9_out);
  not not_9 (not_9_out, B);
  not not_10 (not_10_out, A);
  not not_11 (not_11_out, C);
  and and_6 (and_6_out, not_10_out, not_11_out, not_12_out);
  not not_12 (not_12_out, D);
  not not_13 (not_13_out, B);
  and and_7 (and_7_out, not_13_out, not_14_out);
  not not_14 (not_14_out, C);
  not not_15 (not_15_out, A);
  and and_8 (and_8_out, not_15_out, C, D);
  not not_16 (not_16_out, B);
  and and_9 (and_9_out, not_16_out, not_17_out);
  not not_17 (not_17_out, C);
  not not_18 (not_18_out, A);
  and and_10 (and_10_out, not_18_out, D);
  not not_19 (not_19_out, A);
  and and_11 (and_11_out, not_19_out, B);
  not not_20 (not_20_out, A);
  not not_21 (not_21_out, B);
  not not_22 (not_22_out, D);
  not not_23 (not_23_out, A);
  not not_24 (not_24_out, B);
  not not_25 (not_25_out, A);
  not not_26 (not_26_out, D);
  not not_27 (not_27_out, A);
  not not_28 (not_28_out, C);
  not not_29 (not_29_out, B);
  not not_30 (not_30_out, C);
  not not_31 (not_31_out, B);
  and and_12 (and_12_out, not_31_out, not_32_out, not_33_out);
  not not_32 (not_32_out, C);
  not not_33 (not_33_out, D);
  not not_34 (not_34_out, A);
  and and_13 (and_13_out, not_34_out, C, not_35_out);
  not not_35 (not_35_out, D);
  not not_36 (not_36_out, A);
  not not_37 (not_37_out, C);
  and and_14 (and_14_out, not_36_out, not_37_out, not_38_out);
  not not_38 (not_38_out, D);
  not not_39 (not_39_out, A);
  and and_15 (and_15_out, not_39_out, B, not_40_out);
  not not_40 (not_40_out, C);
  not not_41 (not_41_out, A);
  and and_16 (and_16_out, not_41_out, B, not_42_out);
  not not_42 (not_42_out, D);
  not not_43 (not_43_out, B);
  and and_17 (and_17_out, A, not_43_out, not_44_out);
  not not_44 (not_44_out, C);
  not not_45 (not_45_out, A);
  not not_46 (not_46_out, B);
  and and_18 (and_18_out, not_45_out, not_46_out, C);
  not not_47 (not_47_out, A);
  and and_19 (and_19_out, not_47_out, B, not_48_out);
  not not_48 (not_48_out, C);
  not not_49 (not_49_out, A);
  and and_20 (and_20_out, not_49_out, B, not_50_out);
  not not_50 (not_50_out, D);
  and and_21 (and_21_out, A, not_51_out, not_52_out);
  not not_51 (not_51_out, B);
  not not_52 (not_52_out, C);
  and and_22 (and_22_out, A, C);
  and and_23 (and_23_out, A, B);
  or or_1 (a_2, and_1_out, and_2_out, and_3_out, and_4_out);
  or or_2 (b_2, and_5_out, and_6_out, and_7_out, and_8_out);
  or or_3 (c_2, and_9_out, and_10_out, and_11_out);
  and and_24 (and_24_out, not_20_out, not_21_out, not_22_out);
  and and_25 (and_25_out, not_23_out, not_24_out, C);
  and and_26 (and_26_out, not_25_out, C, not_26_out);
  and and_27 (and_27_out, not_27_out, B, not_28_out, D);
  and and_28 (and_28_out, A, not_29_out, not_30_out);
  or or_4 (e, and_12_out, and_13_out);
  or or_5 (f, and_14_out, and_15_out, and_16_out, and_17_out);
  or or_6 (g, and_18_out, and_19_out, and_20_out, and_21_out);
  or or_7 (pt, and_22_out, and_23_out);
  or or_8 (d_2, and_24_out, and_25_out, and_26_out, and_27_out, and_28_out);

  // Notes on the sheet:
  //   Anderson Carlos da Silva Morais - 2020010461
endmodule

module ci_relogio (
  output [3:0] h_2,
  output [3:0] h_4,
  output [3:0] min_6,
  output [3:0] min_10,
  output [3:0] seg_6,
  output [3:0] seg_10
);

  wire and_1_out, and_2_out, and_3_out, and_4_out, and_5_out, and_6_out, and_7_out, clock_1_out, not_2_out,
       or_1_out;

  Clock clock_1 (.out(clock_1_out));
  and and_1 (and_1_out, h_2[1], h_4[2]);
  not not_1 (h_2[3], 1'b1);
  J_K_Flip_Flop #(.trigger("falling")) j_k_ff_1 (
    .J(1'b1), .clk(h_2[0]), .K(1'b1), .Q(h_2[1]), .en(1'b1), .reset(and_1_out));  // open: Qn, preset
  J_K_Flip_Flop #(.trigger("falling")) j_k_ff_2 (
    .J(1'b1), .clk(and_3_out), .K(1'b1), .Q(h_2[0]), .en(1'b1), .reset(and_1_out));  // open: Qn, preset
  and and_2 (and_2_out, h_4[3], h_4[1]);
  not not_2 (not_2_out, and_1_out);
  or or_1 (or_1_out, and_1_out, and_2_out);
  and and_3 (and_3_out, not_2_out, or_1_out);
  J_K_Flip_Flop #(.trigger("falling")) j_k_ff_3 (
    .J(1'b1), .clk(h_4[2]), .K(1'b1), .Q(h_4[3]), .en(1'b1), .reset(or_1_out));  // open: Qn, preset
  J_K_Flip_Flop #(.trigger("falling")) j_k_ff_4 (
    .J(1'b1), .clk(h_4[1]), .K(1'b1), .Q(h_4[2]), .en(1'b1), .reset(or_1_out));  // open: Qn, preset
  J_K_Flip_Flop #(.trigger("falling")) j_k_ff_5 (
    .J(1'b1), .clk(h_4[0]), .K(1'b1), .Q(h_4[1]), .en(1'b1), .reset(or_1_out));  // open: Qn, preset
  J_K_Flip_Flop #(.trigger("falling")) j_k_ff_6 (
    .J(1'b1), .clk(and_4_out), .K(1'b1), .Q(h_4[0]), .en(1'b1), .reset(or_1_out));  // open: Qn, preset
  and and_4 (and_4_out, min_6[2], min_6[1]);
  J_K_Flip_Flop #(.trigger("falling")) j_k_ff_7 (
    .J(1'b1), .clk(min_6[1]), .K(1'b1), .Q(min_6[2]), .en(1'b1), .reset(and_4_out));  // open: Qn, preset
  J_K_Flip_Flop #(.trigger("falling")) j_k_ff_8 (
    .J(1'b1), .clk(min_6[0]), .K(1'b1), .Q(min_6[1]), .en(1'b1), .reset(and_4_out));  // open: Qn, preset
  J_K_Flip_Flop #(.trigger("falling")) j_k_ff_9 (
    .J(1'b1), .clk(and_5_out), .K(1'b1), .Q(min_6[0]), .en(1'b1), .reset(and_4_out));  // open: Qn, preset
  and and_5 (and_5_out, min_10[3], min_10[1]);
  J_K_Flip_Flop #(.trigger("falling")) j_k_ff_10 (
    .J(1'b1), .clk(min_10[2]), .K(1'b1), .Q(min_10[3]), .en(1'b1), .reset(and_5_out));  // open: Qn, preset
  J_K_Flip_Flop #(.trigger("falling")) j_k_ff_11 (
    .J(1'b1), .clk(min_10[1]), .K(1'b1), .Q(min_10[2]), .en(1'b1), .reset(and_5_out));  // open: Qn, preset
  J_K_Flip_Flop #(.trigger("falling")) j_k_ff_12 (
    .J(1'b1), .clk(min_10[0]), .K(1'b1), .Q(min_10[1]), .en(1'b1), .reset(and_5_out));  // open: Qn, preset
  J_K_Flip_Flop #(.trigger("falling")) j_k_ff_13 (
    .J(1'b1), .clk(and_6_out), .K(1'b1), .Q(min_10[0]), .en(1'b1), .reset(and_5_out));  // open: Qn, preset
  and and_6 (and_6_out, seg_6[2], seg_6[1]);
  J_K_Flip_Flop #(.trigger("falling")) j_k_ff_14 (
    .J(1'b1), .clk(seg_6[1]), .K(1'b1), .Q(seg_6[2]), .en(1'b1), .reset(and_6_out));  // open: Qn, preset
  J_K_Flip_Flop #(.trigger("falling")) j_k_ff_15 (
    .J(1'b1), .clk(seg_6[0]), .K(1'b1), .Q(seg_6[1]), .en(1'b1), .reset(and_6_out));  // open: Qn, preset
  J_K_Flip_Flop #(.trigger("falling")) j_k_ff_16 (
    .J(1'b1), .clk(and_7_out), .K(1'b1), .Q(seg_6[0]), .en(1'b1), .reset(and_6_out));  // open: Qn, preset
  and and_7 (and_7_out, seg_10[3], seg_10[1]);
  J_K_Flip_Flop #(.trigger("falling")) j_k_ff_17 (
    .J(1'b1), .clk(seg_10[2]), .K(1'b1), .Q(seg_10[3]), .en(1'b1), .reset(and_7_out));  // open: Qn, preset
  J_K_Flip_Flop #(.trigger("falling")) j_k_ff_18 (
    .J(1'b1), .clk(seg_10[1]), .K(1'b1), .Q(seg_10[2]), .en(1'b1), .reset(and_7_out));  // open: Qn, preset
  J_K_Flip_Flop #(.trigger("falling")) j_k_ff_19 (
    .J(1'b1), .clk(seg_10[0]), .K(1'b1), .Q(seg_10[1]), .en(1'b1), .reset(and_7_out));  // open: Qn, preset
  J_K_Flip_Flop #(.trigger("falling")) j_k_ff_20 (
    .J(1'b1), .clk(clock_1_out), .K(1'b1), .Q(seg_10[0]), .en(1'b1), .reset(and_7_out));  // open: Qn, preset

  assign h_2[2] = h_2[3];
  assign min_6[3] = h_2[3];
  assign seg_6[3] = h_2[3];

  // Notes on the sheet:
  //   sinal 0 para portas não usadas
  //   Anderson Carlos da Silva Morais - 2020010461
  //   Lógica para zerar os dois digitos de 24h
  //   24h
  //   60min
  //   60s
endmodule

module ci_distribuidor (
  output [3:0] seg_10_up,
  output [3:0] seg6up,
  output [3:0] seg10dwn,
  output [3:0] seg6dwn,
  output [3:0] min10up,
  output [3:0] min6up,
  output [3:0] min10dwn,
  output [3:0] min6dwn,
  output [3:0] h4up,
  output [3:0] h2up,
  output [3:0] h4dwn,
  output [3:0] h2dwn
);

  wire [3:0] Circuito_de_horas_h_2, Circuito_de_horas_h_4, Circuito_de_horas_min_6, Circuito_de_horas_min_10,
       Circuito_de_horas_seg_6, Circuito_de_horas_seg_10;

  ci_relogio Circuito_de_horas (
    .h_2(Circuito_de_horas_h_2), .h_4(Circuito_de_horas_h_4), .min_6(Circuito_de_horas_min_6),
    .min_10(Circuito_de_horas_min_10), .seg_6(Circuito_de_horas_seg_6), .seg_10(Circuito_de_horas_seg_10));
  ci_display seg_10 (
    .A(Circuito_de_horas_seg_10[3]), .B(Circuito_de_horas_seg_10[2]), .C(Circuito_de_horas_seg_10[1]),
    .D(Circuito_de_horas_seg_10[0]), .a_2(seg_10_up[1]), .b_2(seg_10_up[0]), .c_2(seg10dwn[2]),
    .d_2(seg10dwn[1]), .e(seg10dwn[0]), .f(seg_10_up[2]), .g(seg_10_up[3]), .pt(seg10dwn[3]));
  ci_display min_10 (
    .A(Circuito_de_horas_min_10[3]), .B(Circuito_de_horas_min_10[2]), .C(Circuito_de_horas_min_10[1]),
    .D(Circuito_de_horas_min_10[0]), .a_2(min10up[1]), .b_2(min10up[0]), .c_2(min10dwn[2]),
    .d_2(min10dwn[1]), .e(min10dwn[0]), .f(min10up[2]), .g(min10up[3]));  // open: pt
  ci_display h_4 (
    .A(Circuito_de_horas_h_4[3]), .B(Circuito_de_horas_h_4[2]), .C(Circuito_de_horas_h_4[1]),
    .D(Circuito_de_horas_h_4[0]), .a_2(h4up[1]), .b_2(h4up[0]), .c_2(h4dwn[2]), .d_2(h4dwn[1]), .e(h4dwn[0]),
    .f(h4up[2]), .g(h4up[3]));  // open: pt
  ci_display seg_6 (
    .A(Circuito_de_horas_seg_6[3]), .B(Circuito_de_horas_seg_6[2]), .C(Circuito_de_horas_seg_6[1]),
    .D(Circuito_de_horas_seg_6[0]), .a_2(seg6up[1]), .b_2(seg6up[0]), .c_2(seg6dwn[2]), .d_2(seg6dwn[1]),
    .e(seg6dwn[0]), .f(seg6up[2]), .g(seg6up[3]), .pt(seg6dwn[3]));
  ci_display min_6 (
    .A(Circuito_de_horas_min_6[3]), .B(Circuito_de_horas_min_6[2]), .C(Circuito_de_horas_min_6[1]),
    .D(Circuito_de_horas_min_6[0]), .a_2(min6up[1]), .b_2(min6up[0]), .c_2(min6dwn[2]), .d_2(min6dwn[1]),
    .e(min6dwn[0]), .f(min6up[2]), .g(min6up[3]), .pt(min6dwn[3]));
  ci_display h_2 (
    .A(Circuito_de_horas_h_2[3]), .B(Circuito_de_horas_h_2[2]), .C(Circuito_de_horas_h_2[1]),
    .D(Circuito_de_horas_h_2[0]), .a_2(h2up[1]), .b_2(h2up[0]), .c_2(h2dwn[2]), .d_2(h2dwn[1]), .e(h2dwn[0]),
    .f(h2up[2]), .g(h2up[3]), .pt(h2dwn[3]));

  assign h4dwn[3] = 1'b1;
  assign min10dwn[3] = 1'b1;

  // Notes on the sheet:
  //   Ponto como separador de hh:mm:ss
  //   Anderson Carlos da Silva Morais - 2020010461
  //   Circuito distribuidor
endmodule

module \relógio  (
);

  wire [3:0] Circuito_distribuidor_h2dwn, Circuito_distribuidor_h2up, Circuito_distribuidor_h4dwn,
       Circuito_distribuidor_h4up, Circuito_distribuidor_min6dwn, Circuito_distribuidor_min6up,
       Circuito_distribuidor_min10dwn, Circuito_distribuidor_min10up, Circuito_distribuidor_seg6dwn,
       Circuito_distribuidor_seg6up, Circuito_distribuidor_seg10dwn, Circuito_distribuidor_seg_10_up;

  ci_distribuidor Circuito_distribuidor (
    .seg_10_up(Circuito_distribuidor_seg_10_up), .seg6up(Circuito_distribuidor_seg6up),
    .seg10dwn(Circuito_distribuidor_seg10dwn), .seg6dwn(Circuito_distribuidor_seg6dwn),
    .min10up(Circuito_distribuidor_min10up), .min6up(Circuito_distribuidor_min6up),
    .min10dwn(Circuito_distribuidor_min10dwn), .min6dwn(Circuito_distribuidor_min6dwn),
    .h4up(Circuito_distribuidor_h4up), .h2up(Circuito_distribuidor_h2up),
    .h4dwn(Circuito_distribuidor_h4dwn), .h2dwn(Circuito_distribuidor_h2dwn));
  _7_Segment_Display u_7_segment_display_1 (
    .g(Circuito_distribuidor_h2up[3]), .f(Circuito_distribuidor_h2up[2]), .a(Circuito_distribuidor_h2up[1]),
    .b(Circuito_distribuidor_h2up[0]), .e(Circuito_distribuidor_h2dwn[0]),
    .d(Circuito_distribuidor_h2dwn[1]), .c(Circuito_distribuidor_h2dwn[2]),
    .dp(Circuito_distribuidor_h2dwn[3]));
  _7_Segment_Display u_7_segment_display_2 (
    .g(Circuito_distribuidor_h4up[3]), .f(Circuito_distribuidor_h4up[2]), .a(Circuito_distribuidor_h4up[1]),
    .b(Circuito_distribuidor_h4up[0]), .e(Circuito_distribuidor_h4dwn[0]),
    .d(Circuito_distribuidor_h4dwn[1]), .c(Circuito_distribuidor_h4dwn[2]),
    .dp(Circuito_distribuidor_h4dwn[3]));
  _7_Segment_Display u_7_segment_display_3 (
    .g(Circuito_distribuidor_min6up[3]), .f(Circuito_distribuidor_min6up[2]),
    .a(Circuito_distribuidor_min6up[1]), .b(Circuito_distribuidor_min6up[0]),
    .e(Circuito_distribuidor_min6dwn[0]), .d(Circuito_distribuidor_min6dwn[1]),
    .c(Circuito_distribuidor_min6dwn[2]), .dp(Circuito_distribuidor_min6dwn[3]));
  _7_Segment_Display u_7_segment_display_4 (
    .g(Circuito_distribuidor_min10up[3]), .f(Circuito_distribuidor_min10up[2]),
    .a(Circuito_distribuidor_min10up[1]), .b(Circuito_distribuidor_min10up[0]),
    .e(Circuito_distribuidor_min10dwn[0]), .d(Circuito_distribuidor_min10dwn[1]),
    .c(Circuito_distribuidor_min10dwn[2]), .dp(Circuito_distribuidor_min10dwn[3]));
  _7_Segment_Display u_7_segment_display_5 (
    .g(Circuito_distribuidor_seg_10_up[3]), .f(Circuito_distribuidor_seg_10_up[2]),
    .a(Circuito_distribuidor_seg_10_up[1]), .b(Circuito_distribuidor_seg_10_up[0]),
    .e(Circuito_distribuidor_seg10dwn[0]), .d(Circuito_distribuidor_seg10dwn[1]),
    .c(Circuito_distribuidor_seg10dwn[2]), .dp(Circuito_distribuidor_seg10dwn[3]));
  _7_Segment_Display u_7_segment_display_6 (
    .g(Circuito_distribuidor_seg6up[3]), .f(Circuito_distribuidor_seg6up[2]),
    .a(Circuito_distribuidor_seg6up[1]), .b(Circuito_distribuidor_seg6up[0]),
    .e(Circuito_distribuidor_seg6dwn[0]), .d(Circuito_distribuidor_seg6dwn[1]),
    .c(Circuito_distribuidor_seg6dwn[2]), .dp(Circuito_distribuidor_seg6dwn[3]));

  // Notes on the sheet:
  //   Anderson Carlos da Silva Morais - 2020010461
  //   mostrador
endmodule
