// Logisim project ConversaoGreyBinario.circ as structural Verilog: 1 circuit, main circuit main
module main (
  input  B0,
  input  G0,
  input  B1,
  input  G1,
  input  B2,
  input  G2,
  input  B3,
  input  G3,
  input  B0_2,
  input  G0_2,
  input  B1_2,
  input  G1_2,
  input  B2_2,
  input  B3_2,
  input  G2_2,
  input  G3_2,
  output G0_3,
  output B0_3,
  output G1_3,
  output B1_3,
  output G2_3,
  output B2_3,
  output G3_3,
  output B3_3,
  output G0_4,
  output B0_4,
  output G1_4,
  output B1_4,
  output G2_4,
  output G3_4,
  output B2_4,
  output B3_4
);

  xor xor_1 (G0_3, B0, B1);
  xor xor_2 (G1_3, B1, B2);
  xor xor_3 (G2_3, B2, B3);
  xor xor_4 (G0_4, B0_2, B1_2);
  xor xor_5 (G1_4, B1_2, B2_2);
  xor xor_6 (G2_4, B2_2, B3_2);
  xor xor_7 (B0_3, G0, B1_3);
  xor xor_8 (B1_3, G1, B2_3);
  xor xor_9 (B2_3, G2, G3);
  xor xor_10 (B0_4, G0_2, B1_4);
  xor xor_11 (B1_4, G1_2, B2_4);
  xor xor_12 (B2_4, G2_2, G3_2);

  assign B3_3 = G3;
  assign B3_4 = G3_2;
  assign G3_3 = B3;
  assign G3_4 = B3_2;

  // Notes on the sheet:
  //   Binário para Grey
  //   Binário para Grey
  //   Grey para Binário
  //   Grey para Binário
endmodule
