// Logisim project DecodificadorEnable.circ as structural Verilog: 1 circuit, main circuit main
module main (
  input  in_1,
  input  in_2,
  input  in_3,
  input  A2,
  input  A1,
  input  A0,
  output Q0,
  output Q1,
  output Q2,
  output Q3,
  output Q4,
  output Q5,
  output Q6,
  output Q7
);

  wire and_7_out;

  and and_1 (Q0, and_7_out, ~A2, ~A1, ~A0);  // AND_Gate
  and and_2 (Q1, and_7_out, ~A2, ~A1, A0);  // AND_Gate
  and and_3 (Q2, and_7_out, ~A2, A1, ~A0);  // AND_Gate
  and and_4 (Q3, and_7_out, ~A2, A1, A0);  // AND_Gate
  and and_5 (Q4, and_7_out, A2, ~A1, ~A0);  // AND_Gate
  and and_6 (Q5, and_7_out, A2, ~A1, A0);  // AND_Gate
  and and_7 (and_7_out, ~in_1, ~in_2, in_3);  // AND_Gate
  and and_8 (Q7, and_7_out, A2, A1, A0);
  and and_9 (Q6, and_7_out, A2, A1, ~A0);  // AND_Gate

  // Notes on the sheet:
  //   Decodificador com Enable
endmodule
