// Logisim project MuxDemux.circ as structural Verilog: 1 circuit, main circuit main
module main (
  input  in_1,
  input  in_2,
  input  in_3,
  input  in_4,
  input  in_5,
  input  in_6,
  input  in_7,
  input  in_8,
  input  in_9,
  input  [2:0] in_10,
  input  in_11,
  input  [2:0] in_12,
  input  in_13,
  input  in_14,
  input  in_15,
  input  in_16,
  input  in_17,
  input  in_18,
  input  in_19,
  input  in_20,
  input  [2:0] in_21,
  input  [2:0] in_22,
  output out_23,
  output out_24,
  output out_25,
  output out_26,
  output out_27,
  output out_28,
  output out_29,
  output out_30,
  output out_31,
  output out_32,
  output out_33
);

  Multiplexer #(.select(3), .enable("false")) multiplexer_1 (
    .in0(in_2), .in1(in_3), .in2(in_4), .in3(in_5), .in4(in_6), .in5(in_7), .in6(in_8), .in7(in_9),
    .out(out_24), .sel(in_12));
  Multiplexer #(.select(3), .enable("false")) multiplexer_2 (
    .in0(in_13), .in1(in_14), .in2(in_15), .in3(in_16), .in4(in_17), .in5(in_18), .in6(in_19), .in7(in_20),
    .out(out_27), .sel(in_21));
  Demultiplexer #(.select(3), .enable("false")) demultiplexer_1 (
    .out0(out_25), .out1(out_26), .out2(out_28), .out3(out_29), .out4(out_30), .out5(out_31), .out6(out_32),
    .out7(out_33), .in(out_27), .sel(in_22));
  Multiplexer #(.select(3), .enable("false")) multiplexer_3 (
    .in0(in_11), .in1(in_11), .in2(in_1), .in3(in_1), .in4(in_1), .in5(in_1), .in6(in_11), .in7(in_1),
    .out(out_23), .sel(in_10));

  // Notes on the sheet:
  //   Seletor
  //   Roteamento de bits
  //   Tabela-verdade
  //   Seletor
endmodule
