// Logisim project pratica_04.circ as structural Verilog: 1 circuit, main circuit main
module main (
  input  in_1
);

  wire and_1_out, clock_1_out, j_k_ff_1_q, j_k_ff_2_q, j_k_ff_3_q, j_k_ff_4_q, j_k_ff_9_p4, j_k_ff_9_p5,
       j_k_ff_14_p5, j_k_ff_19_p5, j_k_ff_25_p5, undriven, undriven_2, undriven_3, undriven_4, undriven_5,
       undriven_6, undriven_7, undriven_8;
  wire [3:3] j_k_ff_9_p1;

  Clock clock_1 (.out(clock_1_out));
  and and_1 (and_1_out, j_k_ff_3_q, j_k_ff_1_q);
  J_K_Flip_Flop #(.trigger("falling")) j_k_ff_1 (
    .J(in_1), .clk(j_k_ff_2_q), .K(in_1), .Q(j_k_ff_1_q), .reset(and_1_out));  // open: Qn, preset
  J_K_Flip_Flop #(.trigger("falling")) j_k_ff_2 (
    .J(in_1), .clk(j_k_ff_3_q), .K(in_1), .Q(j_k_ff_2_q), .reset(and_1_out));  // open: Qn, preset
  J_K_Flip_Flop #(.trigger("falling")) j_k_ff_3 (
    .J(in_1), .clk(j_k_ff_4_q), .K(in_1), .Q(j_k_ff_3_q), .reset(and_1_out));  // open: Qn, preset
  J_K_Flip_Flop #(.trigger("falling")) j_k_ff_4 (
    .J(in_1), .clk(clock_1_out), .K(in_1), .Q(j_k_ff_4_q), .reset(and_1_out));  // open: Qn, preset
  J_K_Flip_Flop #(.trigger("falling")) j_k_ff_5 (
    .J(j_k_ff_9_p1[3]), .K(undriven), .clk(undriven_2), .preset(j_k_ff_9_p1[3]), .reset(j_k_ff_9_p1[3]));  // open: Q, Qn
  J_K_Flip_Flop #(.trigger("falling")) j_k_ff_6 (
    .J(j_k_ff_9_p1[3]), .K(undriven), .clk(undriven_2), .preset(j_k_ff_9_p1[3]));  // open: Q, Qn, reset
  J_K_Flip_Flop #(.trigger("falling")) j_k_ff_7 (
    .preset(j_k_ff_9_p1[3]), .reset(j_k_ff_9_p1[3]));  // open: J, K, clk, Q, Qn
  J_K_Flip_Flop #(.trigger("falling")) j_k_ff_8 (
    .K(j_k_ff_9_p5), .preset(j_k_ff_9_p1[3]));  // open: J, clk, Q, Qn, reset
  // J_K_Flip_Flop #(.trigger("falling")) j_k_ff_9: pin names not known; wires that end beside it: j_k_ff_9_p1[3], j_k_ff_9_p1[3], j_k_ff_9_p1[3], j_k_ff_9_p4, j_k_ff_9_p5, j_k_ff_9_p1[3]
  J_K_Flip_Flop #(.trigger("falling")) j_k_ff_10 (
    .J(j_k_ff_9_p1[3]), .K(undriven_3), .clk(undriven_4), .preset(j_k_ff_9_p1[3]), .reset(j_k_ff_9_p1[3]));  // open: Q, Qn
  J_K_Flip_Flop #(.trigger("falling")) j_k_ff_11 (
    .preset(j_k_ff_9_p1[3]), .reset(j_k_ff_9_p1[3]));  // open: J, K, clk, Q, Qn
  J_K_Flip_Flop #(.trigger("falling")) j_k_ff_12 (
    .J(j_k_ff_9_p1[3]), .K(undriven_3), .clk(undriven_4), .preset(j_k_ff_9_p1[3]));  // open: Q, Qn, reset
  J_K_Flip_Flop #(.trigger("falling")) j_k_ff_13 (
    .K(j_k_ff_14_p5), .preset(j_k_ff_9_p1[3]));  // open: J, clk, Q, Qn, reset
  // J_K_Flip_Flop #(.trigger("falling")) j_k_ff_14: pin names not known; wires that end beside it: j_k_ff_9_p1[3], j_k_ff_9_p1[3], j_k_ff_9_p1[3], j_k_ff_9_p4, j_k_ff_14_p5, j_k_ff_9_p1[3]
  J_K_Flip_Flop #(.trigger("falling")) j_k_ff_15 (
    .J(j_k_ff_9_p1[3]), .K(undriven_5), .clk(undriven_6), .preset(j_k_ff_9_p1[3]), .reset(j_k_ff_9_p1[3]));  // open: Q, Qn
  J_K_Flip_Flop #(.trigger("falling")) j_k_ff_16 (
    .J(j_k_ff_9_p1[3]), .K(undriven_5), .clk(undriven_6), .preset(j_k_ff_9_p1[3]));  // open: Q, Qn, reset
  J_K_Flip_Flop #(.trigger("falling")) j_k_ff_17 (
    .preset(j_k_ff_9_p1[3]), .reset(j_k_ff_9_p1[3]));  // open: J, K, clk, Q, Qn
  J_K_Flip_Flop #(.trigger("falling")) j_k_ff_18 (
    .K(j_k_ff_19_p5), .preset(j_k_ff_9_p1[3]));  // open: J, clk, Q, Qn, reset
  // J_K_Flip_Flop #(.trigger("falling")) j_k_ff_19: pin names not known; wires that end beside it: j_k_ff_9_p1[3], j_k_ff_9_p1[3], j_k_ff_9_p1[3], j_k_ff_9_p4, j_k_ff_19_p5, j_k_ff_9_p1[3]
  J_K_Flip_Flop #(.trigger("falling")) j_k_ff_20 (
    .J(j_k_ff_9_p1[3]), .preset(j_k_ff_9_p1[3]), .reset(j_k_ff_9_p1[3]));  // open: K, clk, Q, Qn
  J_K_Flip_Flop #(.trigger("falling")) j_k_ff_21 (
    .J(j_k_ff_9_p1[3]), .K(undriven_7), .clk(undriven_8), .preset(j_k_ff_9_p1[3]));  // open: Q, Qn, reset
  J_K_Flip_Flop #(.trigger("falling")) j_k_ff_22 (
    .J(j_k_ff_9_p1[3]), .K(undriven_7), .clk(undriven_8), .preset(j_k_ff_9_p1[3]));  // open: Q, Qn, reset
  J_K_Flip_Flop #(.trigger("falling")) j_k_ff_23 (
    .preset(j_k_ff_9_p1[3]), .reset(j_k_ff_9_p1[3]));  // open: J, K, clk, Q, Qn
  J_K_Flip_Flop #(.trigger("falling")) j_k_ff_24 (
    .K(j_k_ff_25_p5), .preset(j_k_ff_9_p1[3]));  // open: J, clk, Q, Qn, reset
  // J_K_Flip_Flop #(.trigger("falling")) j_k_ff_25: pin names not known; wires that end beside it: j_k_ff_9_p1[3], j_k_ff_9_p1[3], j_k_ff_9_p1[3], j_k_ff_9_p4, j_k_ff_25_p5, j_k_ff_9_p1[3]

  // Notes on the sheet:
  //   gerador de clock
  //   Anderson Carlos da Silva Morais
  //   Marilia Fonsêca Andrade
endmodule
