// Logisim project pratica_06.circ as structural Verilog: 1 circuit, main circuit main
module main (
  input  M1,
  input  M2,
  input  M3,
  input  M4,
  output S1,
  output S2,
  output S3,
  output S4
);

  wire and_1_out, and_2_out, and_3_out, and_4_out, and_5_out, and_6_out, and_7_out, and_8_out, not_1_out,
       not_2_out, not_3_out, not_4_out, not_5_out, not_6_out, not_7_out, not_8_out, or_2_out;

  not not_1 (not_1_out, M1);
  and and_1 (and_1_out, not_1_out, M3);
  not not_2 (not_2_out, M2);
  and and_2 (and_2_out, not_2_out, M3);
  not not_3 (not_3_out, M1);
  and and_3 (and_3_out, not_3_out, not_4_out);
  not not_4 (not_4_out, M2);
  not not_5 (not_5_out, M1);
  and and_4 (and_4_out, not_5_out, not_6_out);
  not not_6 (not_6_out, M3);
  not not_7 (not_7_out, M2);
  not not_8 (not_8_out, M3);
  or or_1 (S3, and_1_out, and_2_out);
  and and_5 (and_5_out, and_3_out, M4);
  and and_6 (and_6_out, and_4_out, M4);
  and and_7 (and_7_out, not_7_out, not_8_out);
  or or_2 (or_2_out, and_5_out, and_6_out);
  and and_8 (and_8_out, and_7_out, M4);
  or or_3 (S4, or_2_out, and_8_out);

  assign S1 = M1;
  assign S2 = M2;
endmodule
