// Logisim project pratica_03.circ as structural Verilog: 1 circuit, main circuit main
module main (
  input  x,
  input  y,
  input  z,
  output s
);

  wire and_1_out, and_2_out, and_3_out, or_1_out;

  and and_1 (and_1_out, y, z);
  and and_2 (and_2_out, x, z);
  or or_1 (or_1_out, and_1_out, and_2_out);
  and and_3 (and_3_out, x, y);
  or or_2 (s, or_1_out, and_3_out);

  // Notes on the sheet:
  //   Anderson Carlos da Silva Morais
  //   Marília Fonsêca Andrade
endmodule
