// Logisim project pratica_05_final.circ as structural Verilog: 1 circuit, main circuit main
module main (
  input  H,
  output P,
  output M,
  output out_4,
  output L,
  output Y
);

  wire and_1_out, and_2_out, and_3_out, and_4_out, D0, or_1_out, or_2_out, xor_1_out;

  and and_1 (and_1_out, ~M, D0);  // AND_Gate
  and and_2 (and_2_out, and_1_out, H);
  and and_3 (and_3_out, M, ~D0);  // AND_Gate
  and and_4 (and_4_out, M, ~H);  // AND_Gate
  or or_1 (or_1_out, and_2_out, and_3_out);
  xor xor_1 (xor_1_out, D0, H);
  not not_1 (P, M);
  xor xor_2 (L, M, D0);
  xnor xnor_1 (Y, M, D0);
  or or_2 (or_2_out, or_1_out, and_4_out);
  Clock clock_1 (.out(out_4));
  D_Flip_Flop d_ff_1 (.clk(out_4), .D(or_2_out), .Q(M), .en(1'b1));  // open: Qn, preset, reset
  D_Flip_Flop d_ff_2 (.clk(out_4), .D(xor_1_out), .Q(D0), .en(1'b1));  // open: Qn, preset, reset

  // Other names for the same wires on the sheet: D1 = M
endmodule
