// Logisim project pratica_05_final2.circ as structural Verilog: 1 circuit, main circuit main
module main (
  input  H,
  output P,
  output M,
  output L,
  output Y
);

  wire and_1_out, and_2_out, and_3_out, and_4_out, clock_1_out, D0, nD0, not_1_out, or_1_out, or_2_out,
       xor_1_out;

  not not_1 (not_1_out, H);
  and and_1 (and_1_out, P, D0);
  xor xor_1 (xor_1_out, D0, H);
  xor xor_2 (L, M, D0);
  and and_2 (and_2_out, and_1_out, H);
  and and_3 (and_3_out, M, nD0);
  and and_4 (and_4_out, M, not_1_out);
  not not_2 (Y, L);
  or or_1 (or_1_out, and_2_out, and_3_out);
  or or_2 (or_2_out, or_1_out, and_4_out);
  Clock clock_1 (.out(clock_1_out));
  D_Flip_Flop d_ff_1 (.clk(clock_1_out), .D(or_2_out), .Q(M), .Qn(P), .en(1'b1));  // open: preset, reset
  D_Flip_Flop d_ff_2 (.clk(clock_1_out), .D(xor_1_out), .Q(D0), .Qn(nD0), .en(1'b1));  // open: preset, reset

  // Other names for the same wires on the sheet: D1 = M; nD1 = P
endmodule
