// Logisim project template.circ as structural Verilog: 1 circuit, main circuit main
module main (
  input  E1,
  input  E0,
  input  H,
  output D1,
  output D0,
  output P,
  output M,
  output L,
  output Y
);

  wire and_1_out, and_2_out, and_3_out, and_4_out, and_5_out, and_6_out, and_7_out, and_8_out, and_9_out,
       and_10_out, not_1_out, not_2_out, not_3_out, not_5_out, not_6_out, not_7_out, not_8_out, not_9_out,
       not_10_out, or_4_out;

  not not_1 (not_1_out, E1);
  not not_2 (not_2_out, E0);
  not not_3 (not_3_out, H);
  not not_4 (P, E1);
  not not_5 (not_5_out, E1);
  not not_6 (not_6_out, E0);
  not not_7 (not_7_out, E1);
  not not_8 (not_8_out, E0);
  and and_1 (and_1_out, not_1_out, E0);
  not not_9 (not_9_out, E0);
  and and_2 (and_2_out, not_2_out, H);
  and and_3 (and_3_out, E0, not_3_out);
  and and_4 (and_4_out, not_5_out, E0);
  and and_5 (and_5_out, E1, not_6_out);
  and and_6 (and_6_out, not_7_out, not_8_out);
  and and_7 (and_7_out, E1, E0);
  and and_8 (and_8_out, and_1_out, H);
  and and_9 (and_9_out, E1, not_9_out);
  not not_10 (not_10_out, H);
  or or_1 (D0, and_2_out, and_3_out);
  or or_2 (L, and_4_out, and_5_out);
  or or_3 (Y, and_6_out, and_7_out);
  or or_4 (or_4_out, and_8_out, and_9_out);
  and and_10 (and_10_out, E1, not_10_out);
  or or_5 (D1, or_4_out, and_10_out);

  assign M = E1;
endmodule
